// Logisim project t1.circ as structural Verilog: 2 circuits, main circuit Tarea1
module Tarea1 (
  input  X0,
  input  X1,
  input  X2,
  input  X3,
  output out_5
);

  wire and_1_out, and_2_out, and_3_out, and_4_out, and_5_out, and_6_out, not_1_out, not_2_out, not_3_out;

  not not_1 (not_1_out, X2);
  not not_2 (not_2_out, X3);
  not not_3 (not_3_out, X0);
  // NOT_Gate not_4 has open pins: in=X1, out=open
  and and_1 (and_1_out, X0, X1);
  and and_2 (and_2_out, X0, X2);
  and and_3 (and_3_out, X2, X3);
  and and_4 (and_4_out, X0, not_1_out, X3);
  and and_5 (and_5_out, X3, not_3_out, X1);
  and and_6 (and_6_out, X1, X2, not_2_out);
  or or_1 (out_5, and_1_out, and_2_out, and_3_out, and_4_out, and_5_out, and_6_out);
endmodule

module t1 (
  input  x0,
  input  x1,
  input  x2,
  input  x3,
  output a
);

  wire and_1_out, and_2_out, and_3_out, and_4_out, and_5_out, and_6_out, not_1_out, not_2_out, not_3_out,
       not_4_out, not_5_out, not_6_out, not_7_out, not_8_out, not_9_out, not_10_out, not_11_out, not_12_out;

  not not_1 (not_1_out, x0);
  and and_1 (and_1_out, not_1_out, not_2_out);
  not not_2 (not_2_out, x1);
  not not_3 (not_3_out, x0);
  and and_2 (and_2_out, not_3_out, not_4_out);
  not not_4 (not_4_out, x2);
  not not_5 (not_5_out, x0);
  and and_3 (and_3_out, not_5_out, not_6_out);
  not not_6 (not_6_out, x3);
  not not_7 (not_7_out, x1);
  and and_4 (and_4_out, not_7_out, not_8_out);
  not not_8 (not_8_out, x2);
  not not_9 (not_9_out, x1);
  and and_5 (and_5_out, not_9_out, not_10_out);
  not not_10 (not_10_out, x3);
  not not_11 (not_11_out, x2);
  and and_6 (and_6_out, not_11_out, not_12_out);
  not not_12 (not_12_out, x3);
  or or_1 (a, and_1_out, and_2_out, and_3_out, and_4_out, and_5_out, and_6_out);
endmodule
