// Logisim project t2.circ as structural Verilog: 4 circuits, main circuit main
module main (
  input  X0,
  input  X1,
  output Z
);

  wire clock_1_out, clock_2_out, d0_1_d0, d1_1_d1, register_1_q, register_2_q;

  // Probe on register_2_q
  // Probe on register_1_q
  Z z_1 (.Q0(register_1_q), .Q1(register_2_q), .X0(X0), .X1(X1), .Z(Z));
  D0 d0_1 (.X0(X0), .X1(X1), .Q0(register_1_q), .Q1(register_2_q), .D0(d0_1_d0));
  Clock clock_1 (.out(clock_1_out));
  D1 d1_1 (.X0(X0), .X1(X1), .Q0(register_1_q), .Q1(register_2_q), .D1(d1_1_d1));
  Clock clock_2 (.out(clock_2_out));
  Register #(.width(1), .trigger("falling")) register_1 (
    .D(d0_1_d0), .Q(register_1_q), .clk(clock_1_out));  // open: en, clr
  Register #(.width(1), .trigger("falling")) register_2 (
    .D(d1_1_d1), .Q(register_2_q), .clk(clock_2_out));  // open: en, clr
endmodule

module D0 (
  input  X0,
  input  X1,
  input  Q0,
  input  Q1,
  output D0
);

  wire and_1_out, and_2_out, not_1_out, not_2_out;

  not not_1 (not_1_out, Q0);
  not not_2 (not_2_out, Q1);
  and and_1 (and_1_out, X1, not_1_out);
  and and_2 (and_2_out, not_1_out, X0, not_2_out);
  or or_1 (D0, and_1_out, and_2_out);
endmodule

module D1 (
  input  X0,
  input  X1,
  input  Q0,
  input  Q1,
  output D1
);

  wire and_1_out, and_2_out, and_3_out, not_1_out, not_2_out, not_3_out, not_4_out;

  not not_1 (not_1_out, X0);
  not not_2 (not_2_out, X1);
  not not_3 (not_3_out, Q0);
  not not_4 (not_4_out, Q1);
  and and_1 (and_1_out, not_1_out, not_2_out, not_4_out);
  and and_2 (and_2_out, not_3_out, Q1, X1);
  and and_3 (and_3_out, Q0, not_4_out);
  or or_1 (D1, and_1_out, and_2_out, and_3_out);
endmodule

module Z (
  input  Q0,
  input  Q1,
  input  X0,
  input  X1,
  output Z
);


  assign Z = Q1;
endmodule
