// Logisim project t3.circ as structural Verilog: 1 circuit, main circuit main
module main (
  input  [7:0] D,
  input  START,
  output READY,
  output ERROR,
  output [2:0] out_5
);

  wire clock_1_out, comparator_1_eq, not_1_out, or_1_out;
  wire [2:0] adder_1_out, multiplexer_2_out, Z_q;
  wire [7:0] multiplexer_3_out, register_1_q, shifter_1_out, shifter_2_out;

  Clock clock_1 (.out(clock_1_out));
  Comparator comparator_1 (.a(D), .b({8{1'b0}}), .eq(comparator_1_eq));  // open: gt, lt
  Shifter #(.shift("lr")) shifter_1 (.in(D), .\dist (3'b001), .out(shifter_1_out));
  Multiplexer multiplexer_1 (.in0(1'b0), .in1(1'b1), .out(ERROR), .sel(comparator_1_eq));  // open: en
  Shifter #(.shift("lr")) shifter_2 (.in(register_1_q), .\dist (3'b001), .out(shifter_2_out));
  Multiplexer #(.width(3)) multiplexer_2 (
    .in0(adder_1_out), .in1(3'b000), .out(multiplexer_2_out), .sel(START));  // open: en
  Multiplexer #(.width(8)) multiplexer_3 (
    .in0(shifter_2_out), .in1(shifter_1_out), .out(multiplexer_3_out), .sel(START));  // open: en
  // Probe on multiplexer_2_out
  or or_1 (or_1_out, START, not_1_out);
  Register #(.trigger("falling")) register_1 (
    .D(multiplexer_3_out), .Q(register_1_q), .clk(clock_1_out));  // open: en, clr
  Register #(.width(3), .trigger("falling")) Z (
    .D(multiplexer_2_out), .en(or_1_out), .Q(Z_q), .clk(clock_1_out));  // open: clr
  Adder #(.width(3)) adder_1 (.a(Z_q), .b(3'b001), .out(adder_1_out));  // open: cin, cout
  // Probe on Z_q
  // Probe on Z_q
  // Probe on adder_1_out
  not not_1 (not_1_out, READY);
  // Probe on register_1_q
  Comparator comparator_2 (.a(register_1_q), .b({8{1'b0}}), .eq(READY));  // open: gt, lt
  Multiplexer #(.width(3)) multiplexer_4 (.in1(Z_q), .out(out_5), .sel(READY));  // open: in0, en
endmodule
